# Fritzing sketch DoorSensor (saved by Fritzing 0.9.2b)
breadboards: 1

parts:
  Raspberry_Pi1 = Raspberry Pi B+
  S1 = Reed switch [package=THT]
  R1 = Resistor [tolerance=±5% resistance=1k package=THT]

nets:
  N1: Raspberry_Pi1.3v3, S1.pin_1
  N2: Raspberry_Pi1.GPIO3, Raspberry_Pi1.GND, R1.Pin_0
  N3: Raspberry_Pi1.GPIO4, S1.pin_2, R1.Pin_1
